// Logisim project logisim1-22-08.circ as structural Verilog: 1 circuit, main circuit main
module main (
  input  X,
  input  Y,
  input  X_2,
  input  Y_2,
  input  in_5,
  input  in_6,
  output OUTPUT,
  output out_8,
  output out_9
);

  wire and_1_out, and_3_out, not_1_out, not_2_out;

  not not_1 (not_1_out, X);
  not not_2 (not_2_out, Y);
  and and_1 (and_1_out, not_1_out, Y);
  and and_2 (out_8, X_2, Y_2);
  xor xor_1 (out_9, in_5, in_6);
  and and_3 (and_3_out, not_2_out, X);
  or or_1 (OUTPUT, and_1_out, and_3_out);

  // Notes on the sheet:
  //   NOT GATE
  //   IMPLEMENTING XOR USING AND , OR , NOT GATE
  //   NOT GATE
  //   AND GATE
  //   AND GATE
  //   AND GATE
  //   OR GATE
  //   AND GATE OUTPUT
  //   FUNCTIONAL FORM - X(bar)Y + Y(bar)X
endmodule
